// Logisim project Final Project.circ as structural Verilog: 9 circuits, main circuit main
module main (
  input  DEC,
  input  INC,
  input  [7:0] Clock_Input,
  input  Clear_All,
  output [3:0] ROM_4_7,
  output [3:0] ROM_0_3,
  output [7:0] Clock_Output,
  output [3:0] Reg_0,
  output [3:0] Reg_1,
  output [3:0] ALU_out
);

  wire Clock_out;
  wire [3:0] multiplexer_1_out;
  wire [6:0] rom_2_data;

  Counter counter_1 (
    .load(DEC), .D(Clock_Input), .count(INC), .Q(Clock_Output), .clk(Clock_out), .clr(Clear_All));  // open: carry
  Clock Clock (.out(Clock_out));
  ROM rom_1 (.addr(Clock_Output), .data({ROM_4_7, ROM_0_3}));  // open: sel
  ROM #(.addrWidth(4), .dataWidth(7)) rom_2 (.addr(ROM_4_7), .data(rom_2_data));  // open: sel
  Multiplexer #(.width(4), .enable("false")) multiplexer_1 (
    .in0(ROM_0_3), .in1(ALU_out), .out(multiplexer_1_out), .sel(rom_2_data[3]));
  _4_Bit_Reg_x2 u_4_bit_reg_x2_1 (
    .Input(multiplexer_1_out), .Clear(Clear_All), ._1_Bit_Select(rom_2_data[1]), .Clock(Clock_out),
    .WE(rom_2_data[0]), .Out_0(Reg_0), .Out_1(Reg_1));
  TTY #(.rows(2), .cols(27)) tty_1 (.data({Reg_0[2:0], Reg_1}), .clk(Clock_out), .we(rom_2_data[2]), .clr(Clear_All));
  ALU alu_1 (
    .A_In(Reg_0), .B_In(Reg_1), .Add_Sub(rom_2_data[3]), .Clear(Clear_All), ._2_Bit_Select(rom_2_data[6:5]),
    .WE(rom_2_data[4]), .Clock(Clock_out), .Output(ALU_out));

  // Notes on the sheet:
  //   contents of rom_1 (hex, n*v repeats v):
  //   0 14 28 30 16 25 30 16 2c 30 16 2c 30 16 2f 30 12 20 30 14 22 30 14 2e 30 12 20 30 13 23 30 12 2b 30
  //   13 24 30 60 13 2d 30 50 30 12 20 30 13 23 30 12 2a 30 13 23 30 60 40 60 13 2d 30 50 30 12 20 30 13
  //   24 30 10 60 12 2d 30 13 23 30 13 2d 30 40 60 50 13 30 12 20 30 13 24 30 10 60 12 2d 30 13 23 30 40
  //   a0 13 2d 30 50 13 30 12 20 30 14 22 30 17 29 30 12 20 30 14 2a 30 16 2f 30 16 2e 30 16 21 30 17 24
  //   30 16 28 30 16 21 30 16 2e 30 12 20 30 14 23 30 16 21 30 17 22 30 16 2c 30 17 23 30 16 2f 30 16 2e
  //   30
  //   PROM
  //   contents of rom_2 (hex, n*v repeats v):
  //   0 1 3 4 9 b 10 a 30 78 18
  //   Decoder
  //   Register
  //   ALU
endmodule

module _1_Bit_Adder (
  input  I0,
  input  I1,
  input  I2,
  output Sum,
  output CO
);

  wire and_1_out, and_2_out, xor_1_out;

  xor xor_1 (xor_1_out, I0, I1);
  xor xor_2 (Sum, xor_1_out, I2);
  and and_1 (and_1_out, I2, xor_1_out);
  or or_1 (CO, and_1_out, and_2_out);
  and and_2 (and_2_out, I1, I0);

  // Notes on the sheet:
  //   1-Bit Adder
endmodule

module _4_bit_Adder (
  input  A3,
  input  A2,
  input  A1,
  input  A0,
  input  Add_Sub,
  input  B3,
  input  B2,
  input  B1,
  input  B0,
  output O3,
  output O2,
  output O1,
  output O0,
  output Carry_Out
);

  wire n1_bit_adder_1_co, n1_bit_adder_2_co, n1_bit_adder_3_co, xor_1_out, xor_2_out, xor_3_out, xor_4_out;

  xor xor_1 (xor_1_out, Add_Sub, B3);
  xor xor_2 (xor_2_out, Add_Sub, B2);
  xor xor_3 (xor_3_out, Add_Sub, B1);
  _1_Bit_Adder u_1_bit_adder_1 (.I0(A0), .I1(xor_4_out), .I2(Add_Sub), .Sum(O0), .CO(n1_bit_adder_1_co));
  _1_Bit_Adder u_1_bit_adder_2 (.I0(A1), .I1(xor_3_out), .I2(n1_bit_adder_1_co), .Sum(O1), .CO(n1_bit_adder_2_co));
  _1_Bit_Adder u_1_bit_adder_3 (.I0(A2), .I1(xor_2_out), .I2(n1_bit_adder_2_co), .Sum(O2), .CO(n1_bit_adder_3_co));
  _1_Bit_Adder u_1_bit_adder_4 (.I0(A3), .I1(xor_1_out), .I2(n1_bit_adder_3_co), .Sum(O3), .CO(Carry_Out));
  xor xor_4 (xor_4_out, Add_Sub, B0);
endmodule

module _4_Bit_register (
  input  Q0,
  input  Clear,
  input  Q1,
  input  Q2,
  input  Q3,
  input  WE,
  input  Clock,
  output O0,
  output O1,
  output O2,
  output O3
);

  wire multiplexer_1_out, multiplexer_2_out, multiplexer_3_out, multiplexer_4_out;

  Multiplexer #(.enable("false")) multiplexer_1 (.in0(O0), .in1(Q0), .out(multiplexer_1_out), .sel(WE));
  Multiplexer #(.enable("false")) multiplexer_2 (.in0(O1), .in1(Q1), .out(multiplexer_2_out), .sel(WE));
  Multiplexer #(.enable("false")) multiplexer_3 (.in0(O2), .in1(Q2), .out(multiplexer_3_out), .sel(WE));
  Multiplexer #(.enable("false")) multiplexer_4 (.in0(O3), .in1(Q3), .out(multiplexer_4_out), .sel(WE));
  D_Flip_Flop d_ff_1 (.clk(Clock), .D(multiplexer_1_out), .Q(O0), .reset(Clear));  // open: Qn, preset, en
  D_Flip_Flop d_ff_2 (.clk(Clock), .D(multiplexer_2_out), .Q(O1), .reset(Clear));  // open: Qn, preset, en
  D_Flip_Flop d_ff_3 (.clk(Clock), .D(multiplexer_3_out), .Q(O2), .reset(Clear));  // open: Qn, preset, en
  D_Flip_Flop d_ff_4 (.clk(Clock), .D(multiplexer_4_out), .Q(O3), .reset(Clear));  // open: Qn, preset, en
endmodule

module _4_Bit_Reg_x2 (
  input  Clear,
  input  [3:0] Input,
  input  _1_Bit_Select,
  input  Clock,
  input  WE,
  output [3:0] Out_0,
  output [3:0] Out_1
);

  wire [3:0] multiplexer_1_out, multiplexer_2_out;

  Multiplexer #(.width(4), .enable("false")) multiplexer_1 (
    .in0(Input), .in1(Out_0), .out(multiplexer_1_out), .sel(_1_Bit_Select));
  Multiplexer #(.width(4), .enable("false")) multiplexer_2 (
    .in0(Out_1), .in1(Input), .out(multiplexer_2_out), .sel(_1_Bit_Select));
  _4_Bit_register Reg_0 (
    .Q0(multiplexer_1_out[0]), .Q1(multiplexer_1_out[1]), .Q2(multiplexer_1_out[2]),
    .Q3(multiplexer_1_out[3]), .Clear(Clear), .WE(WE), .Clock(Clock), .O0(Out_0[0]), .O1(Out_0[1]),
    .O2(Out_0[2]), .O3(Out_0[3]));
  _4_Bit_register Reg_1 (
    .Q0(multiplexer_2_out[0]), .Q1(multiplexer_2_out[1]), .Q2(multiplexer_2_out[2]),
    .Q3(multiplexer_2_out[3]), .Clear(Clear), .WE(WE), .Clock(Clock), .O0(Out_1[0]), .O1(Out_1[1]),
    .O2(Out_1[2]), .O3(Out_1[3]));
endmodule

module Bitwise_AND (
  input  [3:0] A_In,
  input  [3:0] B_In,
  output O0,
  output O1,
  output O2,
  output O3
);

  and and_1 (O0, A_In[0], B_In[0]);
  and and_2 (O1, A_In[1], B_In[1]);
  and and_3 (O2, A_In[2], B_In[2]);
  and and_4 (O3, A_In[3], B_In[3]);
endmodule

module Bitwise_OR (
  input  [3:0] A_In,
  input  [3:0] B_In,
  output O0,
  output O1,
  output O2,
  output O3
);

  or or_1 (O0, A_In[0], B_In[0]);
  or or_2 (O1, A_In[1], B_In[1]);
  or or_3 (O2, A_In[2], B_In[2]);
  or or_4 (O3, A_In[3], B_In[3]);
endmodule

module Bitwise_XOR (
  input  [3:0] A_In,
  input  [3:0] B_In,
  output O0,
  output O1,
  output O2,
  output O3
);

  xor xor_1 (O0, A_In[0], B_In[0]);
  xor xor_2 (O1, A_In[1], B_In[1]);
  xor xor_3 (O2, A_In[2], B_In[2]);
  xor xor_4 (O3, A_In[3], B_In[3]);
endmodule

module ALU (
  input  [3:0] A_In,
  input  [3:0] B_In,
  input  Add_Sub,
  input  Clear,
  input  [1:0] _2_Bit_Select,
  input  WE,
  input  Clock,
  output [3:0] Output
);

  wire [3:0] Adder_o0, AND_o0, multiplexer_1_out, OR_o0, XOR_o0;

  _4_bit_Adder Adder (
    .A3(A_In[3]), .A2(A_In[2]), .A1(A_In[1]), .A0(A_In[0]), .B3(B_In[3]), .B2(B_In[2]), .B1(B_In[1]),
    .B0(B_In[0]), .Add_Sub(Add_Sub), .O3(Adder_o0[3]), .O2(Adder_o0[2]), .O1(Adder_o0[1]), .O0(Adder_o0[0]));  // open: Carry_Out
  Bitwise_OR OR (.A_In(A_In), .B_In(B_In), .O0(OR_o0[0]), .O1(OR_o0[1]), .O2(OR_o0[2]), .O3(OR_o0[3]));
  Bitwise_AND AND (.A_In(A_In), .B_In(B_In), .O0(AND_o0[0]), .O1(AND_o0[1]), .O2(AND_o0[2]), .O3(AND_o0[3]));
  Bitwise_XOR XOR (.A_In(A_In), .B_In(B_In), .O0(XOR_o0[0]), .O1(XOR_o0[1]), .O2(XOR_o0[2]), .O3(XOR_o0[3]));
  Multiplexer #(.select(2), .width(4), .enable("false")) multiplexer_1 (
    .in0(Adder_o0), .in1(OR_o0), .in2(AND_o0), .in3(XOR_o0), .out(multiplexer_1_out), .sel(_2_Bit_Select));
  _4_Bit_register u_4_bit_register_1 (
    .Q0(multiplexer_1_out[0]), .Q1(multiplexer_1_out[1]), .Q2(multiplexer_1_out[2]),
    .Q3(multiplexer_1_out[3]), .Clear(Clear), .WE(WE), .Clock(Clock), .O0(Output[0]), .O1(Output[1]),
    .O2(Output[2]), .O3(Output[3]));
endmodule
