// Logisim project wesley.circ as structural Verilog: 2 circuits, main circuit sd
module sd (
  input  in_1,
  output out_2,
  output out_3
);

  wire and_1_out, and_2_out, clock_1_out, not_1_out;

  Clock clock_1 (.out(clock_1_out));
  not not_1 (not_1_out, in_1);
  and and_1 (and_1_out, not_1_out, clock_1_out);
  and and_2 (and_2_out, clock_1_out, in_1);
  nor nor_1 (out_2, and_1_out, out_3);
  nor nor_2 (out_3, out_2, and_2_out);
endmodule

module adg (
  input  in_1,
  output out_2
);


  assign out_2 = in_1;
endmodule
